// Logisim project ipc.circ as structural Verilog: 2 circuits, main circuit main
module main (
);

  wire add_out, adder_1_cout, alu_out, and_2_out, and_3_out, and_4_out, and_5_out, and_6_out, and_7_out,
       and_8_out, and_9_out, and_10_out, and_11_out, and_12_out, and_13_out, and_14_out, and_15_out,
       and_16_out, and_17_out, and_18_out, and_19_out, and_20_out, and_21_out, and_22_out, and_23_out,
       and_24_out, and_25_out, and_26_out, and_27_out, and_28_out, and_29_out, and_31_out, and_32_out,
       and_33_out, and_34_out, and_35_out, and_36_out, and_37_out, button_1_out, button_2_out, button_3_out,
       button_4_out, button_5_out, button_6_out, carryt, clock_1_out, clockt, decoder_1_out0, decoder_1_out1,
       decoder_1_out2, decoder_1_out3, decoder_1_out4, decoder_1_out5, decoder_1_out6, decoder_1_out7,
       decoder_1_out8, decoder_1_out9, decoder_1_out10, decoder_1_out11, decoder_1_out12, decoder_1_out13,
       decoder_1_out14, decoder_1_out15, decoder_1_out16, decoder_1_out17, decoder_1_out18, decoder_1_out19,
       decoder_1_out20, decoder_1_out21, decoder_1_out22, decoder_1_out23, decoder_1_out29, decoder_1_out30,
       decoder_2_out1, decoder_2_out2, decoder_3_out0, decoder_3_out1, decoder_3_out2, decoder_3_out3,
       decoder_3_out4, decoder_3_out5, decoder_3_out6, decoder_3_out7, in_sig, ld, nor_2_out, nor_3_out,
       nor_4_out, nor_5_out, not_1_out, not_2_out, or_1_out, or_2_out, or_3_out, or_4_out, or_5_out,
       or_6_out, or_7_out, out_sig, parityt, register_in_out, register_out_out, setting_carry_out, signt,
       str, sub_out, undriven, using_adder_out, xor_2_out, xor_10_out, zerot;
  wire [1:0] counter_2_q;
  wire [2:0] multiplexer_1_out, register_1_q;
  wire [7:0] ac, adder_1_out, and_30_out, controlled_buffer_13_out, inputd, mah, mal, multiplexer_2_out,
       multiplexer_3_out, multiplexer_4_out, multiplexer_5_out, nor_1_out, opcode, out_d,
       pull_resistor_1_node, r1, r2, r3, r4, ram_1_data, sf, sp, xor_1_out;
  wire [15:0] counter_1_q;

  Clock clock_1 (.out(clock_1_out));
  and and_1 (clockt, ~decoder_1_out29, clock_1_out);  // AND_Gate
  Counter #(.max('hffff), .trigger("falling"), .width(16)) counter_1 (
    .load(or_2_out), .D({mah, mal}), .count(1'b1), .Q(counter_1_q), .up(1'b1), .clk(clockt));  // open: carry, clr
  ROM #(.addrWidth(16)) rom_1 (.addr(counter_1_q), .data(opcode));
  RAM #(.addrWidth(16), .databus("bidir"), .enables("line")) ram_1 (
    .addr({mah, mal}), .data(ram_1_data));  // open: we, oe, clk
  not not_1 (not_1_out, decoder_2_out1);
  Decoder #(.select(5)) decoder_1 (
    .out0(decoder_1_out0), .out1(decoder_1_out1), .out2(decoder_1_out2), .out3(decoder_1_out3),
    .out4(decoder_1_out4), .out5(decoder_1_out5), .out6(decoder_1_out6), .out7(decoder_1_out7),
    .out8(decoder_1_out8), .out9(decoder_1_out9), .out10(decoder_1_out10), .out11(decoder_1_out11),
    .out12(decoder_1_out12), .out13(decoder_1_out13), .out14(decoder_1_out14), .out15(decoder_1_out15),
    .out16(decoder_1_out16), .out17(decoder_1_out17), .out18(decoder_1_out18), .out19(decoder_1_out19),
    .out20(decoder_1_out20), .out21(decoder_1_out21), .out22(decoder_1_out22), .out23(decoder_1_out23),
    .out24(str), .out25(ld), .out26(in_sig), .out27(out_sig), .out29(decoder_1_out29),
    .out30(decoder_1_out30), .sel(opcode[4:0]), .en(not_1_out));  // open: out28, out31
  Register #(.width(3)) register_1 (.D(opcode[7:5]), .en(1'b1), .clk(clockt), .Q(register_1_q));  // open: clr
  and and_2 (and_2_out, decoder_1_out14, carryt);
  and and_3 (and_3_out, decoder_1_out15, ~carryt);  // AND_Gate
  and and_4 (and_4_out, decoder_1_out16, zerot);
  and and_5 (and_5_out, decoder_1_out17, ~zerot);  // AND_Gate
  and and_6 (and_6_out, decoder_1_out18, signt);
  and and_7 (and_7_out, decoder_1_out19, ~signt);  // AND_Gate
  and and_8 (and_8_out, parityt, decoder_1_out20);
  and and_9 (and_9_out, decoder_1_out21, ~parityt);  // AND_Gate
  or or_1 (or_1_out, decoder_1_out22, decoder_2_out1);
  Multiplexer #(.width(3)) multiplexer_1 (
    .in0(opcode[7:5]), .in1(register_1_q), .out(multiplexer_1_out), .sel(decoder_2_out1));
  Counter #(.max('h3), .trigger("falling"), .width(2)) counter_2 (
    .count(or_1_out), .Q(counter_2_q), .up(1'b1), .clk(clockt), .clr(decoder_2_out2));  // open: load, D, carry
  Decoder #(.enable("false"), .select(2)) decoder_2 (
    .out1(decoder_2_out1), .out2(decoder_2_out2), .sel(counter_2_q));  // open: out0, out3
  Decoder #(.enable("false"), .select(3)) decoder_3 (
    .out0(decoder_3_out0), .out1(decoder_3_out1), .out2(decoder_3_out2), .out3(decoder_3_out3),
    .out4(decoder_3_out4), .out5(decoder_3_out5), .out6(decoder_3_out6), .out7(decoder_3_out7),
    .sel(multiplexer_1_out));
  or or_2 (or_2_out, decoder_1_out13, and_2_out, and_3_out, and_4_out, and_5_out, and_6_out, and_7_out, and_8_out, and_9_out);
  or add (add_out, decoder_1_out0, decoder_1_out30, decoder_1_out2);
  or setting_carry (setting_carry_out, using_adder_out, decoder_1_out4);
  or using_adder (using_adder_out, add_out, sub_out);
  or sub (sub_out, decoder_1_out1, decoder_1_out3, decoder_1_out8);
  or register_out (register_out_out, alu_out, decoder_1_out11, str, out_sig);
  or alu (alu_out, setting_carry_out, decoder_1_out5, decoder_1_out6, decoder_1_out7);
  assign out_d = out_sig ? ram_1_data : 8'bz;  // Controlled_Buffer controlled_buffer_1
  and and_10 (and_10_out, decoder_3_out7, register_out_out);
  and and_11 (and_11_out, register_in_out, decoder_3_out7);
  and and_12 (and_12_out, decoder_3_out6, register_out_out);
  and and_13 (and_13_out, register_in_out, decoder_3_out6);
  and and_14 (and_14_out, decoder_3_out5, register_out_out);
  and and_15 (and_15_out, register_in_out, decoder_3_out5);
  and and_16 (and_16_out, decoder_3_out4, register_out_out);
  and and_17 (and_17_out, register_in_out, decoder_3_out4);
  and and_18 (and_18_out, decoder_3_out3, register_out_out);
  and and_19 (and_19_out, register_in_out, decoder_3_out3);
  and and_20 (and_20_out, decoder_3_out2, register_out_out);
  and and_21 (and_21_out, register_in_out, decoder_3_out2);
  and and_22 (and_22_out, decoder_3_out1, register_out_out);
  and and_23 (and_23_out, register_in_out, decoder_3_out1);
  and and_24 (and_24_out, decoder_3_out0, register_out_out);
  and and_25 (and_25_out, decoder_3_out0, register_in_out);
  assign ram_1_data = decoder_2_out1 ? opcode : 8'bz;  // Controlled_Buffer controlled_buffer_2
  or register_in (register_in_out, decoder_2_out1, decoder_1_out12, ld, in_sig);
  Register marh (.D(ram_1_data), .en(and_11_out), .clk(clockt), .Q(mah));  // open: clr
  Register marl (.D(ram_1_data), .en(and_13_out), .clk(clockt), .Q(mal));  // open: clr
  Register u_r3 (.D(multiplexer_2_out), .en(or_3_out), .clk(clockt), .Q(r4));  // open: clr
  Multiplexer #(.width(8)) multiplexer_2 (
    .in0(ram_1_data), .in1(counter_1_q[15:8]), .out(multiplexer_2_out), .sel(decoder_1_out23));
  or or_3 (or_3_out, decoder_1_out23, and_15_out);
  Register u_r2 (.D(multiplexer_3_out), .en(or_4_out), .clk(clockt), .Q(r3));  // open: clr
  Multiplexer #(.width(8)) multiplexer_3 (
    .in0(ram_1_data), .in1(counter_1_q[7:0]), .out(multiplexer_3_out), .sel(decoder_1_out23));
  or or_4 (or_4_out, decoder_1_out23, and_17_out);
  Register u_sp (.D(ram_1_data), .en(and_19_out), .clk(clockt), .Q(sp));  // open: clr
  Register u_r4 (.D(ram_1_data), .en(and_21_out), .clk(clockt), .Q(sf));  // open: clr
  Register u_r1 (.D(ram_1_data), .en(and_23_out), .clk(clockt), .Q(r2));  // open: clr
  Register r0 (.D(ram_1_data), .en(and_25_out), .clk(clockt), .Q(r1));  // open: clr
  Register u_ac (.D(multiplexer_4_out), .en(and_26_out), .clk(clockt), .Q(ac));  // open: clr
  Multiplexer #(.width(8)) multiplexer_4 (
    .in0(ram_1_data), .in1(controlled_buffer_13_out), .out(multiplexer_4_out), .sel(alu_out));
  and and_26 (and_26_out, ~decoder_1_out30, or_5_out);  // AND_Gate
  or or_5 (or_5_out, alu_out, decoder_1_out11);
  assign ram_1_data = in_sig ? inputd : 8'bz;  // Controlled_Buffer controlled_buffer_3
  assign ram_1_data = and_10_out ? mah : 8'bz;  // Controlled_Buffer controlled_buffer_4
  assign ram_1_data = and_12_out ? mal : 8'bz;  // Controlled_Buffer controlled_buffer_5
  assign ram_1_data = and_14_out ? r4 : 8'bz;  // Controlled_Buffer controlled_buffer_6
  assign ram_1_data = and_16_out ? r3 : 8'bz;  // Controlled_Buffer controlled_buffer_7
  assign ram_1_data = and_18_out ? sp : 8'bz;  // Controlled_Buffer controlled_buffer_8
  assign ram_1_data = and_20_out ? sf : 8'bz;  // Controlled_Buffer controlled_buffer_9
  assign ram_1_data = and_22_out ? r2 : 8'bz;  // Controlled_Buffer controlled_buffer_10
  assign ram_1_data = and_24_out ? r1 : 8'bz;  // Controlled_Buffer controlled_buffer_11
  assign ram_1_data = decoder_1_out12 ? ac : 8'bz;  // Controlled_Buffer controlled_buffer_12
  Pull_Resistor pull_resistor_1 (.node(pull_resistor_1_node));
  Multiplexer #(.width(8)) multiplexer_5 (.in0(ac), .in1(pull_resistor_1_node), .out(multiplexer_5_out));  // open: sel
  Pull_Resistor pull_resistor_2 (.node(ram_1_data));
  and and_27 (and_27_out, carryt, decoder_1_out3);
  xor xor_1 (xor_1_out[0], ram_1_data[0], sub_out);
  and and_28 (and_28_out, decoder_1_out2, carryt);
  xor xor_2 (xor_2_out, and_27_out, sub_out);
  and and_29 (and_29_out, xor_2_out, sub_out);
  xor xor_3 (xor_1_out[1], ram_1_data[1], sub_out);
  xor xor_4 (xor_1_out[2], ram_1_data[2], sub_out);
  or or_6 (or_6_out, and_28_out, and_29_out);
  Adder adder_1 (.a(multiplexer_5_out), .b(xor_1_out), .out(adder_1_out), .cin(or_6_out), .cout(adder_1_cout));
  xor xor_5 (xor_1_out[3], ram_1_data[3], sub_out);
  xor xor_6 (xor_1_out[4], ram_1_data[4], sub_out);
  assign controlled_buffer_13_out = decoder_1_out4 ? {carryt, ram_1_data[7:1]} : 8'bz;  // Controlled_Buffer controlled_buffer_13
  assign nor_1_out = ~(ram_1_data | multiplexer_5_out);  // NOR_Gate nor_1, 8 bits wide
  assign controlled_buffer_13_out = decoder_1_out5 ? nor_1_out : 8'bz;  // Controlled_Buffer controlled_buffer_14
  assign and_30_out = ram_1_data & multiplexer_5_out;  // AND_Gate and_30, 8 bits wide
  assign controlled_buffer_13_out = decoder_1_out6 ? and_30_out : 8'bz;  // Controlled_Buffer controlled_buffer_15
  assign controlled_buffer_13_out = using_adder_out ? adder_1_out : 8'bz;  // Controlled_Buffer controlled_buffer_16
  xor xor_7 (xor_1_out[5], ram_1_data[5], sub_out);
  xor xor_8 (xor_1_out[6], ram_1_data[6], sub_out);
  xor xor_9 (xor_1_out[7], ram_1_data[7], sub_out);
  xor xor_10 (xor_10_out, adder_1_cout, sub_out);
  and and_31 (and_31_out, ram_1_data[0], not_2_out);
  not not_2 (not_2_out, using_adder_out);
  nor nor_2 (nor_2_out, controlled_buffer_13_out[7], controlled_buffer_13_out[6]);
  nor nor_3 (nor_3_out, controlled_buffer_13_out[5], controlled_buffer_13_out[4]);
  and and_32 (and_32_out, nor_2_out, nor_3_out);
  and and_33 (and_33_out, and_32_out, and_35_out);
  and and_34 (and_34_out, xor_10_out, using_adder_out);
  or or_7 (or_7_out, and_34_out, and_31_out);
  nor nor_4 (nor_4_out, controlled_buffer_13_out[3], controlled_buffer_13_out[2]);
  nor nor_5 (nor_5_out, controlled_buffer_13_out[1], controlled_buffer_13_out[0]);
  and and_35 (and_35_out, nor_4_out, nor_5_out);
  and and_36 (and_36_out, alu_out, clockt);
  and and_37 (and_37_out, setting_carry_out, clockt);
  Pull_Resistor pull_resistor_3 (.node(controlled_buffer_13_out));
  // Probe on r1
  // Probe on sp
  // Probe on opcode
  D_Flip_Flop carryf (
    .D(or_7_out), .clk(and_37_out), .Q(carryt), .preset(decoder_1_out9), .reset(decoder_1_out10));  // open: Qn
  D_Flip_Flop zerof (.D(and_33_out), .clk(and_36_out), .Q(zerot));  // open: Qn, preset, reset
  D_Flip_Flop signf (.D(controlled_buffer_13_out[7]), .clk(and_36_out), .Q(signt));  // open: Qn, preset, reset
  D_Flip_Flop parityf (.D(controlled_buffer_13_out[0]), .clk(and_36_out), .Q(parityt));  // open: Qn, preset, reset
  DotMatrix #(.matrixcols(8), .matrixrows(8)) dotmatrix_1 (.col0(8'h1));  // open: col1, col2, col3, col4, col5, col6, col7
  input_cont input_cont_1 (
    .in_0(button_1_out), .in_1(button_3_out), .in_2(button_2_out), .in_3(button_4_out), .in_4(button_5_out),
    .in_sig(in_sig), .in_5(button_6_out), .clock_input(clockt), .input_data(inputd));
  Button button_1 (.out(button_1_out));
  Button button_2 (.out(button_2_out));
  Button button_3 (.out(button_3_out));
  Button button_4 (.out(button_4_out));
  // Probe on r2
  // Probe on sf
  // Probe on ac
  Button button_5 (.out(button_5_out));
  // Probe on r3
  // Probe on mal
  LED led_1 (.in(undriven));
  Button button_6 (.out(button_6_out));
  // Probe on r4
  // Probe on mah

  // Notes on the sheet:
  //   contents of rom_1 (hex, n*v repeats v):
  //   1a 1e f6 0 d6 0 10 b6 4 ab 6 f6 0 d6 30 11 b6 8 ab 6 f6 0 d6 3a 11 b6 1 ab 6 f6 0 d6 44 11 b6 2 ab 6
  //   f6 0 d6 4c 11 f6 0 d6 0 d b6 1 ab 20 2c f6 0 d6 0 d b6 1 2b a1 2c f6 0 d6 0 d 2b 20 2c f6 0 d6 0 d a
  //   24 2c f6 0 d6 0 d
  //   Current Byte Immediate?
  //   A
  //   B
  //   ROR
  //   Carry is set by Adder or ROR
endmodule

module input_cont (
  input  in_sig,
  input  clock_input,
  input  in_0,
  input  in_1,
  input  in_2,
  input  in_3,
  input  in_4,
  input  in_5,
  output [7:0] input_data
);

  wire and_1_out, or_1_out;
  wire [7:0] multiplexer_1_out, or_2_out, pull_resistor_1_node, pull_resistor_3_node, register_1_q;
  wire [7:6] pull_resistor_2_node;

  or or_1 (or_1_out, in_0, in_1, in_2, in_3, in_4, in_5);
  Pull_Resistor pull_resistor_1 (.node(pull_resistor_1_node));
  assign or_2_out = {pull_resistor_2_node, in_5, in_4, in_3, in_2, in_1, in_0} | register_1_q;  // OR_Gate or_2, 8 bits wide
  Pull_Resistor pull_resistor_2 (.node({pull_resistor_2_node, in_5, in_4, in_3, in_2, in_1, in_0}));
  and and_1 (and_1_out, ~or_1_out, in_sig);  // AND_Gate
  Register #(.trigger("falling")) register_1 (
    .D(multiplexer_1_out), .en(1'b1), .clk(clock_input), .Q(register_1_q));  // open: clr
  Multiplexer #(.width(8)) multiplexer_1 (
    .in0(or_2_out), .in1(pull_resistor_1_node), .out(multiplexer_1_out));  // open: sel
  Pull_Resistor pull_resistor_3 (.node(pull_resistor_3_node));
  // Probe on register_1_q
  Multiplexer #(.width(8)) multiplexer_2 (
    .in0(pull_resistor_3_node), .in1(register_1_q), .out(input_data));  // open: sel
endmodule
