// Logisim project ipc_ttl.circ as structural Verilog: 2 circuits, main circuit main
module main (
  input  in_1
);

  wire CLK, n7404_1_pin2, n74138_1_pin4, n74138_1_pin6, n74138_1_pin7, n74138_2_pin4, n74138_2_pin6,
       n74138_2_pin7, n74138_3_pin4, n74138_3_pin6, n74138_3_pin7, n74138_4_pin4, n74138_4_pin6,
       n74138_4_pin7, n74139_1_pin1, n74139_1_pin4, n74139_1_pin5, n74139_1_pin6, n74139_1_pin7,
       n74161_1_pin1, n74161_1_pin7, n74161_1_pin10, n74161_2_pin1, n74161_2_pin7, n74161_2_pin10,
       n74161_3_pin1, n74161_3_pin7, n74161_3_pin10, n74161_4_pin1, n74161_4_pin7, n74161_4_pin10, zac;
  wire [3:0] d_register_74173_1_q, d_register_74173_2_q, n74161_1_pin3, n74161_1_pin14, n74161_2_pin3,
       n74161_2_pin14;
  wire [7:0] n74161_4_pin3, n74161_4_pin14, rom_1_data;

  _74161 #(.ShowInternalStructure("true")) u_74161_1 (
    .pin1(n74161_1_pin1), .pin2(CLK), .pin3(n74161_1_pin3[0]), .pin4(n74161_1_pin3[1]),
    .pin5(n74161_1_pin3[2]), .pin6(n74161_1_pin3[3]), .pin7(n74161_1_pin7), .pin14(n74161_1_pin14[0]),
    .pin13(n74161_1_pin14[1]), .pin12(n74161_1_pin14[2]), .pin11(n74161_1_pin14[3]), .pin10(n74161_1_pin10),
    .pin9(in_1));  // open: pin15
  _74161 #(.ShowInternalStructure("true")) u_74161_2 (
    .pin1(n74161_2_pin1), .pin2(CLK), .pin3(n74161_2_pin3[0]), .pin4(n74161_2_pin3[1]),
    .pin5(n74161_2_pin3[2]), .pin6(n74161_2_pin3[3]), .pin7(n74161_2_pin7), .pin15(n74161_1_pin10),
    .pin14(n74161_2_pin14[0]), .pin13(n74161_2_pin14[1]), .pin12(n74161_2_pin14[2]),
    .pin11(n74161_2_pin14[3]), .pin10(n74161_2_pin10), .pin9(in_1));
  ROM #(.addrWidth(16)) rom_1 (.addr({n74161_1_pin14, n74161_2_pin14, n74161_4_pin14}), .data(rom_1_data));
  _74161 #(.ShowInternalStructure("true")) u_74161_3 (
    .pin1(n74161_3_pin1), .pin2(CLK), .pin3(n74161_4_pin3[4]), .pin4(n74161_4_pin3[5]),
    .pin5(n74161_4_pin3[6]), .pin6(n74161_4_pin3[7]), .pin7(n74161_3_pin7), .pin15(n74161_2_pin10),
    .pin14(n74161_4_pin14[4]), .pin13(n74161_4_pin14[5]), .pin12(n74161_4_pin14[6]),
    .pin11(n74161_4_pin14[7]), .pin10(n74161_3_pin10), .pin9(in_1));
  Clock clock_1 (.out(CLK));
  _74161 #(.ShowInternalStructure("true")) u_74161_4 (
    .pin1(n74161_4_pin1), .pin2(CLK), .pin3(n74161_4_pin3[0]), .pin4(n74161_4_pin3[1]),
    .pin5(n74161_4_pin3[2]), .pin6(n74161_4_pin3[3]), .pin7(n74161_4_pin7), .pin15(n74161_3_pin10),
    .pin14(n74161_4_pin14[0]), .pin13(n74161_4_pin14[1]), .pin12(n74161_4_pin14[2]),
    .pin11(n74161_4_pin14[3]), .pin10(n74161_4_pin10), .pin9(in_1));
  d_register_74173 d_register_74173_1 (
    .CLK(CLK), .CLR(n7404_1_pin2), .Q(d_register_74173_1_q));  // open: M, N, G1, G2, D
  d_register_74173 d_register_74173_2 (
    .CLK(CLK), .CLR(n7404_1_pin2), .Q(d_register_74173_2_q));  // open: M, N, G1, G2, D
  _74139 u_74139_1 (
    .pin1(n74139_1_pin1), .pin2(rom_1_data[3]), .pin3(rom_1_data[4]), .pin4(n74139_1_pin4),
    .pin5(n74139_1_pin5), .pin6(n74139_1_pin6), .pin7(n74139_1_pin7));  // open: pin15, pin14, pin13, pin12, pin11, pin10, pin9
  _7404 #(.ShowInternalStructure("true")) u_7404_1 (
    .pin1(zac), .pin2(n7404_1_pin2));  // open: pin3, pin4, pin5, pin6, pin13, pin12, pin11, pin10, pin9, pin8
  _74138 #(.ShowInternalStructure("true")) u_74138_1 (
    .pin1(rom_1_data[0]), .pin2(rom_1_data[1]), .pin3(rom_1_data[2]), .pin4(n74138_1_pin4),
    .pin5(n74139_1_pin4), .pin6(n74138_1_pin6), .pin7(n74138_1_pin7));  // open: pin15, pin14, pin13, pin12, pin11, pin10, pin9
  _74138 #(.ShowInternalStructure("true")) u_74138_2 (
    .pin1(rom_1_data[0]), .pin2(rom_1_data[1]), .pin3(rom_1_data[2]), .pin4(n74138_2_pin4),
    .pin5(n74139_1_pin5), .pin6(n74138_2_pin6), .pin7(n74138_2_pin7));  // open: pin15, pin14, pin13, pin12, pin11, pin10, pin9
  _74138 #(.ShowInternalStructure("true")) u_74138_3 (
    .pin1(rom_1_data[0]), .pin2(rom_1_data[1]), .pin3(rom_1_data[2]), .pin4(n74138_3_pin4),
    .pin5(n74139_1_pin6), .pin6(n74138_3_pin6), .pin7(n74138_3_pin7), .pin11(zac));  // open: pin15, pin14, pin13, pin12, pin10, pin9
  _74138 #(.ShowInternalStructure("true")) u_74138_4 (
    .pin1(rom_1_data[0]), .pin2(rom_1_data[1]), .pin3(rom_1_data[2]), .pin4(n74138_4_pin4),
    .pin5(n74139_1_pin7), .pin6(n74138_4_pin6), .pin7(n74138_4_pin7));  // open: pin15, pin14, pin13, pin12, pin11, pin10, pin9
  // also tied to GND on the sheet: {n74161_4_pin3[0], n74139_1_pin1, n74138_1_pin4, n74138_2_pin4, n74138_3_pin4, n74138_4_pin4}
  // also tied to VCC on the sheet: {n74161_1_pin1, n74161_1_pin7, n74161_2_pin1, n74161_2_pin7, n74161_3_pin1, n74161_4_pin3[1], n74161_4_pin3[2], n74161_4_pin3[3], n74161_4_pin3[4], n74161_4_pin3[5], n74161_4_pin3[6], n74161_4_pin3[7], n74161_2_pin3[0], n74161_2_pin3[1], n74161_2_pin3[2], n74161_2_pin3[3], n74161_1_pin3[0], n74161_1_pin3[1], n74161_1_pin3[2], n74161_1_pin3[3], n74161_3_pin7, n74161_4_pin1, n74161_4_pin10, n74161_4_pin7, n74138_1_pin6, n74138_2_pin6, n74138_3_pin6, n74138_4_pin6}
endmodule

module d_register_74173 (
  input  M,
  input  N,
  input  G1,
  input  G2,
  input  [3:0] D,
  input  CLK,
  input  CLR,
  output [3:0] Q
);

  wire nor_1_out, nor_2_out;
  wire [3:0] register_1_q;

  nor nor_1 (nor_1_out, M, N);
  nor nor_2 (nor_2_out, G1, G2);
  Register #(.width(4)) register_1 (.D(D), .en(nor_2_out), .clk(CLK), .Q(register_1_q), .clr(CLR));
  assign Q = nor_1_out ? register_1_q : 4'bz;  // Controlled_Buffer controlled_buffer_1
endmodule
