// Logisim project rsc1.circ as structural Verilog: 2 circuits, main circuit main
module main (
);

  wire adder_1_cout, and_1_out, and_2_out, and_3_out, and_4_out, and_5_out, and_6_out, and_7_out, and_8_out,
       and_9_out, and_10_out, and_11_out, and_13_out, and_14_out, and_15_out, and_16_out, and_17_out,
       and_18_out, and_19_out, carryf_q, decoder_1_out0, decoder_1_out1, decoder_1_out2, decoder_1_out3,
       decoder_1_out4, decoder_1_out5, decoder_1_out6, decoder_1_out7, decoder_2_out0, decoder_2_out1,
       decoder_2_out2, decoder_2_out3, decoder_2_out4, decoder_2_out5, decoder_2_out6, decoder_2_out8,
       decoder_2_out9, decoder_2_out13, decoder_2_out14, decoder_2_out15, nor_1_out, nor_2_out, nor_3_out,
       nor_5_out, not_1_out, not_2_out, or_1_out, or_2_out, or_3_out, or_4_out, or_5_out, or_6_out, or_7_out,
       or_9_out, or_10_out, or_11_out, xor_1_out;
  wire [2:0] rom_1_data_2;
  wire [3:0] rom_1_data;
  wire [7:0] ac_q, adder_1_out, and_12_out, controlled_buffer_1_out, controlled_buffer_12_out, nor_4_out,
       r1_q, r2_q, r3_q, r4_q, r5_q, r6_q, r7_q, r8_q, ram_1_data, shifter_1_out, xor_9_out;
  wire [7:7] rom_1_data_3;
  wire [15:0] pc_q, undriven;

  Register #(.width(16)) pc (.D(undriven), .Q(pc_q));  // open: en, clk, clr
  ROM #(.addrWidth(16)) rom_1 (.addr(pc_q), .data({rom_1_data_3[7], rom_1_data_2, rom_1_data}));
  RAM #(.addrWidth(16), .databus("bidir"), .enables("line")) ram_1 (
    .addr(undriven), .data(ram_1_data));  // open: we, oe, clk
  Decoder #(.enable("false"), .select(3)) decoder_1 (
    .out0(decoder_1_out0), .out1(decoder_1_out1), .out2(decoder_1_out2), .out3(decoder_1_out3),
    .out4(decoder_1_out4), .out5(decoder_1_out5), .out6(decoder_1_out6), .out7(decoder_1_out7),
    .sel(rom_1_data_2));
  not not_1 (not_1_out, rom_1_data_3[7]);
  Decoder #(.select(4)) decoder_2 (
    .out0(decoder_2_out0), .out1(decoder_2_out1), .out2(decoder_2_out2), .out3(decoder_2_out3),
    .out4(decoder_2_out4), .out5(decoder_2_out5), .out6(decoder_2_out6), .out8(decoder_2_out8),
    .out9(decoder_2_out9), .out13(decoder_2_out13), .out14(decoder_2_out14), .out15(decoder_2_out15),
    .sel(rom_1_data), .en(not_1_out));  // open: out7, out10, out11, out12
  or or_1 (or_1_out, decoder_2_out0, decoder_2_out2);
  or or_2 (or_2_out, or_6_out, decoder_2_out8);
  or or_3 (or_3_out, or_4_out, decoder_2_out4);
  or or_4 (or_4_out, or_1_out, or_5_out);
  or or_5 (or_5_out, decoder_2_out1, decoder_2_out3);
  assign controlled_buffer_1_out = rom_1_data_3[7] ? {rom_1_data_3[7], rom_1_data_2, rom_1_data} : 8'bz;  // Controlled_Buffer controlled_buffer_1
  assign controlled_buffer_1_out = or_2_out ? ram_1_data : 8'bz;  // Controlled_Buffer controlled_buffer_2
  or or_6 (or_6_out, or_3_out, decoder_2_out5, decoder_2_out6);
  and and_1 (and_1_out, decoder_1_out7, or_9_out);
  Register r8 (.D(ram_1_data), .Q(r8_q));  // open: en, clk, clr
  and and_2 (and_2_out, decoder_1_out6, or_9_out);
  Register r7 (.D(ram_1_data), .Q(r7_q));  // open: en, clk, clr
  and and_3 (and_3_out, decoder_1_out5, or_9_out);
  Register r6 (.D(ram_1_data), .Q(r6_q));  // open: en, clk, clr
  and and_4 (and_4_out, decoder_1_out4, or_9_out);
  Register r5 (.D(ram_1_data), .Q(r5_q));  // open: en, clk, clr
  and and_5 (and_5_out, decoder_1_out3, or_9_out);
  Register r4 (.D(ram_1_data), .Q(r4_q));  // open: en, clk, clr
  and and_6 (and_6_out, decoder_1_out2, or_9_out);
  Register r3 (.D(ram_1_data), .Q(r3_q));  // open: en, clk, clr
  and and_7 (and_7_out, decoder_1_out1, or_9_out);
  Register r2 (.D(ram_1_data), .Q(r2_q));  // open: en, clk, clr
  and and_8 (and_8_out, decoder_1_out0, or_9_out);
  Register r1 (.D(ram_1_data), .Q(r1_q));  // open: en, clk, clr
  Register ac (.D(controlled_buffer_1_out), .en(or_7_out), .Q(ac_q));  // open: clk, clr
  or or_7 (or_7_out, or_6_out, rom_1_data_3[7], decoder_2_out14);
  // OR_Gate or_8 has open pins: in0=decoder_2_out9, in1=decoder_2_out14, out=open
  or or_9 (or_9_out, or_6_out, decoder_2_out8, decoder_2_out13, decoder_2_out15);
  nor nor_1 (nor_1_out, controlled_buffer_12_out[7], controlled_buffer_12_out[6]);
  assign ram_1_data = and_1_out ? r8_q : 8'bz;  // Controlled_Buffer controlled_buffer_3
  assign ram_1_data = and_2_out ? r7_q : 8'bz;  // Controlled_Buffer controlled_buffer_4
  assign ram_1_data = and_3_out ? r6_q : 8'bz;  // Controlled_Buffer controlled_buffer_5
  assign ram_1_data = and_4_out ? r5_q : 8'bz;  // Controlled_Buffer controlled_buffer_6
  assign ram_1_data = and_5_out ? r4_q : 8'bz;  // Controlled_Buffer controlled_buffer_7
  assign ram_1_data = and_6_out ? r3_q : 8'bz;  // Controlled_Buffer controlled_buffer_8
  assign ram_1_data = and_7_out ? r2_q : 8'bz;  // Controlled_Buffer controlled_buffer_9
  assign ram_1_data = and_8_out ? r1_q : 8'bz;  // Controlled_Buffer controlled_buffer_10
  assign ram_1_data = decoder_2_out9 ? ac_q : 8'bz;  // Controlled_Buffer controlled_buffer_11
  and and_9 (and_9_out, carryf_q, decoder_2_out3);
  nor nor_2 (nor_2_out, controlled_buffer_12_out[5], controlled_buffer_12_out[4]);
  nor nor_3 (nor_3_out, controlled_buffer_12_out[3], controlled_buffer_12_out[2]);
  and and_10 (and_10_out, nor_1_out, nor_2_out);
  and and_11 (and_11_out, and_10_out, and_13_out);
  xor xor_1 (xor_1_out, and_9_out, or_5_out);
  xor xor_2 (xor_9_out[7], ac_q[0], or_5_out);
  xor xor_3 (xor_9_out[6], ac_q[1], or_5_out);
  assign controlled_buffer_12_out = decoder_2_out4 ? shifter_1_out : 8'bz;  // Controlled_Buffer controlled_buffer_12
  Shifter #(.shift("lr")) shifter_1 (.in(ac_q), .\dist (3'b001), .out(shifter_1_out));
  assign and_12_out = ac_q & ram_1_data;  // AND_Gate and_12, 8 bits wide
  assign controlled_buffer_12_out = decoder_2_out5 ? and_12_out : 8'bz;  // Controlled_Buffer controlled_buffer_13
  assign nor_4_out = ~(ac_q | ram_1_data);  // NOR_Gate nor_4, 8 bits wide
  assign controlled_buffer_12_out = decoder_2_out6 ? nor_4_out : 8'bz;  // Controlled_Buffer controlled_buffer_14
  nor nor_5 (nor_5_out, controlled_buffer_12_out[1], controlled_buffer_12_out[0]);
  and and_13 (and_13_out, nor_3_out, nor_5_out);
  and and_14 (and_14_out, or_1_out, carryf_q);
  or or_10 (or_10_out, and_14_out, and_15_out);
  and and_15 (and_15_out, xor_1_out, or_5_out);
  Adder adder_1 (.a(ram_1_data), .b(xor_9_out), .out(adder_1_out), .cin(or_10_out), .cout(adder_1_cout));
  xor xor_4 (xor_9_out[5], ac_q[2], or_5_out);
  xor xor_5 (xor_9_out[4], ac_q[3], or_5_out);
  assign controlled_buffer_12_out = or_4_out ? adder_1_out : 8'bz;  // Controlled_Buffer controlled_buffer_15
  xor xor_6 (xor_9_out[3], ac_q[4], or_5_out);
  xor xor_7 (xor_9_out[2], ac_q[5], or_5_out);
  xor xor_8 (xor_9_out[1], ac_q[6], or_5_out);
  xor xor_9 (xor_9_out[0], ac_q[7], or_5_out);
  not not_2 (not_2_out, or_4_out);
  and and_16 (and_16_out, adder_1_cout, or_4_out);
  or or_11 (or_11_out, and_16_out, and_17_out);
  and and_17 (and_17_out, ac_q[0], not_2_out);
  D_Flip_Flop carryf (.D(or_11_out), .clk(and_18_out), .Q(carryf_q));  // open: Qn, preset, reset
  buf and_18 (and_18_out, or_3_out);  // AND_Gate
  D_Flip_Flop zerof (.D(and_11_out), .clk(and_19_out));  // open: Q, Qn, preset, reset
  buf and_19 (and_19_out, or_6_out);  // AND_Gate

  // Notes on the sheet:
  //   sub
  //   add
  //   adder
  //   alu
  //   alu_carry
  //   register in
  //   register out
endmodule

module decoding (
);

  wire adder_carry_out, adder_out, alu_out, decoder_1_out0, decoder_1_out1, decoder_1_out2, decoder_1_out3,
       decoder_1_out4, decoder_1_out5, decoder_1_out6, decoder_1_out7, decoder_1_out8, decoder_1_out11,
       decoder_1_out12, decoder_1_out24, decoder_1_out25, decoder_1_out26, decoder_1_out27, no_carry_out;

  Decoder #(.enable("false"), .select(5)) decoder_1 (
    .out0(decoder_1_out0), .out1(decoder_1_out1), .out2(decoder_1_out2), .out3(decoder_1_out3),
    .out4(decoder_1_out4), .out5(decoder_1_out5), .out6(decoder_1_out6), .out7(decoder_1_out7),
    .out8(decoder_1_out8), .out11(decoder_1_out11), .out12(decoder_1_out12), .out24(decoder_1_out24),
    .out25(decoder_1_out25), .out26(decoder_1_out26), .out27(decoder_1_out27));  // open: out9, out10, out13, out14, out15, out16, out17, out18, out19, out20, out21, out22, out23, out28, out29, out30, out31, sel
  or adder (adder_out, no_carry_out, adder_carry_out);
  or no_carry (no_carry_out, decoder_1_out0, decoder_1_out8, decoder_1_out1);
  or adder_carry (adder_carry_out, decoder_1_out2, decoder_1_out3);
  or alu (alu_out, adder_out, decoder_1_out4, decoder_1_out5, decoder_1_out6, decoder_1_out7);
  // OR_Gate register_in has open pins: in0=decoder_1_out12, in1=decoder_1_out25, in2=decoder_1_out26, out=open
  // OR_Gate register_out has open pins: in0=alu_out, in1=decoder_1_out11, in2=decoder_1_out24, in3=decoder_1_out27, out=open
endmodule
